# Fritzing sketch bigcatzero (saved by Fritzing 1.0.8)
breadboards: 3

parts:
  U1 = SWITCH_SPDT [package=kps-1290]
  DRV1 = DollaTek DRV8833
  DRV2 = DollaTek DRV8833
  U3 = ESP 32 DEVKIT DOIT

nets:
  N1: U1.P, DRV1.pin_3, DRV2.pin_3
  N2: DRV1.pin_1, DRV1.pin_2, DRV1.pin_5, DRV1.pin_6, DRV2.pin_1, DRV2.pin_2, DRV2.pin_5, DRV2.pin_6, U3.VP, U3.D33, U3.D25, U3.D26, U3.D27, U3.D14, U3.D12, U3.D13, U3.GND#13, U3.Vin#14
  N3: DRV1.pin_4, DRV2.pin_4

custom parts:
  DollaTek DRV8833: DollaTek DRV8833 1.5A 2-Channel DC Motor Drive Board
